# Fritzing sketch capreravr (saved by Fritzing 0.9.3b)
breadboards: 1

parts:
  DFRobot-DFPlayer-Mini1 = DFRobot-DFPlayer-Mini [part_number=DFR0299]
  R1 = Resistor [tolerance=±5% resistance=1k package=THT]
  R2 = Resistor [tolerance=±5% resistance=1k package=THT]
  SP1 = SPEAKER [package=pcb_mount_speaker]
  R3 = Resistor [tolerance=±5% resistance=10k package=THT]
  C1 = Ceramic Capacitor [capacitance=100nF package="100 mil [THT, multilayer]"]
  S1 = Round Pushbutton
  S2 = Round Pushbutton
  S3 = Round Pushbutton
  C2 = Ceramic Capacitor [capacitance=100nF package="100 mil [THT, multilayer]"]
  R4 = Resistor [tolerance=±5% resistance=10k package=THT]
  R5 = Resistor [tolerance=±5% resistance=10k package=THT]
  C3 = Ceramic Capacitor [capacitance=100nF package="100 mil [THT, multilayer]"]
  C4 = Ceramic Capacitor [capacitance=100nF package="100 mil [THT, multilayer]"]
  R6 = Resistor [tolerance=±5% resistance=220 package=THT]
  S4 = Round Pushbutton
  Part3 = Arduino Uno (Rev3) - ICSP

nets:
  N1: DFRobot-DFPlayer-Mini1.VCC, C1.0, S1.leg1, S2.leg1, S3.leg1, C2.1, R5.Pin_0, C3.0, C4.1, S4.leg1
  N2: DFRobot-DFPlayer-Mini1.RX, R1.Pin_0
  N3: DFRobot-DFPlayer-Mini1.TX, R2.Pin_0
  N4: DFRobot-DFPlayer-Mini1.SPK_1, SP1.-
  N5: DFRobot-DFPlayer-Mini1.GND-1, DFRobot-DFPlayer-Mini1.GND-2, R3.Pin_1, R4.Pin_0, R6.Pin_0
  N6: DFRobot-DFPlayer-Mini1.SPK_2, SP1.+
  N7: DFRobot-DFPlayer-Mini1.BUSY, Part3.D6_PWM
  N8: R1.Pin_1, Part3.ICSP_MOSI, Part3.D11_PWM/MOSI
  N9: R2.Pin_1, Part3.D10_PWM/SS
  N10: R3.Pin_0, C1.1, S1.leg0, Part3.D2
  N11: S2.leg0, R5.Pin_1, C3.1, Part3.D4
  N12: S3.leg0, C2.0, R4.Pin_1, Part3.D3_PWM
  N13: C4.0, R6.Pin_1, S4.leg0, Part3.D5_PWM
